# Fritzing sketch LM2 rev4 wifi (saved by Fritzing 0.9.3b)

parts:
  L298N2 = L298N DC motor driver
  U1 = LIPO-2000mAh [package=lipo-2000]
  M1 = DC Motor
  M2 = DC Motor
  Part2 = Thumb Joystick
  A1 = Arduino UNO R4 WiFi

nets:
  N1: L298N2.OUT1, M1.pin_2
  N2: L298N2.OUT2, M1.pin_1
  N3: L298N2.OUT3, M2.pin_2
  N4: L298N2.OUT4, M2.pin_1
  N5: L298N2.12V, U1.+
  GND: L298N2.GND, U1.-, Part2.GND, A1.Pin_10, A1.Pin_18, A1.Pin_48
  N6: L298N2.5V, A1.Pin_11
  N7: L298N2.ENA, A1.Pin_43
  N8: L298N2.ENB, A1.Pin_37
  N9: L298N2.IN1, A1.Pin_47
  N10: L298N2.IN2, A1.Pin_46
  N11: L298N2.IN3, A1.Pin_45
  N12: L298N2.IN4, A1.Pin_44
  N13: Part2.HORZ, A1.Pin_12
  N14: Part2.VERT, A1.Pin_13
  N15: Part2.VCC, A1.Pin_8

custom parts:
  L298N DC motor driver: 2x DC motor driver with 78M05 positive voltage regulator (7..35 V) L298N: max 46 V, 2 A Set 5 V Enable jumper to enable 5 V regultor (needed for the L298N) and +5 V output at screw terminal or supply external +5 V at screw terminal Set ENA and/or ENB to +5 V to enable motor permanently or supply ENA and/or ENB with PWM signal IN1 and IN2 set rotation directory for motor A (OUT1/OUT2) IN2 and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
  Arduino UNO R4 WiFi: The Arduino UNO R4 WiFi merges the RA4M1 microprocessor from Renesas with the ESP32-S3 from Espressif, creating an all-in-one tool for makers with enhanced processing power and a diverse array of new peripherals.

// code stored in the sketch: LaudoMobile1.ino
//Laudo Lukoki
//Step 1: Make it functional
/*Read and took information from:
https://electrosome.com/interfacing-l298n-motor-driver-arduino-uno/
*/

/* Motor A connections: 
in1 and in2 pins are used to control the direction of Motor A
connected to pin 13, pin 12*/
int enA = 9;
int in1 = 13;
int in2 = 12;
/* Motor B connections: 
in3 and in4 pins are used to control the direction of Motor B
connected to pin 11, pin 10*/
int enB = 3;
int in3 = 11;
int in4 = 10;

//only runs once
void setup() {

    pinMode(enA, OUTPUT);
    pinMode(enB, OUTPUT);
    pinMode(in1, OUTPUT);
    pinMode(in2, OUTPUT);
    pinMode(in3, OUTPUT);
    pinMode(in4, OUTPUT);
	
    digitalWrite(in1, LOW);
    digitalWrite(in2, LOW);
    digitalWrite(in3, LOW);
    digitalWrite(in4, LOW);

    initDrive(100);

    // pinMode(LED_BUILTIN, OUTPUT);
    // //built in led to confirm setup function
    // digitalWrite(LED_BUILTIN, HIGH);
    // delay(1000);
    // digitalWrite(LED_BUILTIN, LOW);
    // delay(500);
    // digitalWrite(LED_BUILTIN, HIGH);
    // delay(1000);
    // digitalWrite(LED_BUILTIN, LOW);
    // delay(500);

}

void loop() {

  
  
    // directionControl();
    // delay(1000);
    // speedControl();
    // delay(1000);
}

void initDrive(int s){
  analogWrite(enA, s);
  analogWrite(enB, s);
 
  // motor A CW ^ (forward)
    digitalWrite(in1, LOW);
    digitalWrite(in2, HIGH);

  // motor B CW ^ (forward)
    digitalWrite(in3, HIGH);
    digitalWrite(in4, LOW);

    delay(1000);

 // Turn off motors
    digitalWrite(in1, LOW);
    digitalWrite(in2, LOW);
    digitalWrite(in3, LOW);
    digitalWrite(in4, LOW);
    delay(2000);


 // motor A CCW (backwards)
    digitalWrite(in1, HIGH);
    digitalWrite(in2, LOW);

  // motor B CCW ^ (backwards)
    digitalWrite(in3, LOW);
    digitalWrite(in4, HIGH);

    delay(1000);

 // Turn off motors
    digitalWrite(in1, LOW);
    digitalWrite(in2, LOW);
    digitalWrite(in3, LOW);
    digitalWrite(in4, LOW);
    delay(2000);
}


//function
void directionControl() {
    // Set motors to maximum speed
    // PWM value ranges from 0 to 255
    analogWrite(enA, 255);
    analogWrite(enB, 255);

    // Turn on motor A & B
    digitalWrite(in1, HIGH);
    digitalWrite(in2, LOW);
    digitalWrite(in3, HIGH);
    digitalWrite(in4, LOW);
    delay(2000);

    digitalWrite(in1, LOW);
    digitalWrite(in2, HIGH);
    digitalWrite(in3, LOW);
    digitalWrite(in4, HIGH);
    delay(2000);
	
    // Turn off motors
    digitalWrite(in1, LOW);
    digitalWrite(in2, LOW);
    digitalWrite(in3, LOW);
    digitalWrite(in4, LOW);
}


void speedControl() {
    // Turn on motors
    digitalWrite(in1, LOW);
    digitalWrite(in2, HIGH);
    digitalWrite(in3, LOW);
    digitalWrite(in4, HIGH);
	
    for (int i = 0; i < 256; i++) {
        analogWrite(enA, i);
        analogWrite(enB, i);
        delay(20);
    }
	
    for (int i = 255; i >= 0; --i) {
        analogWrite(enA, i);
        analogWrite(enB, i);
        delay(20);
    }
	
    // Now turn off motors
    digitalWrite(in1, LOW);
    digitalWrite(in2, LOW);
    digitalWrite(in3, LOW);
    digitalWrite(in4, LOW);
}

/*Set up function to enable wirless connection*/


/*
Concerns:
- very little pmw pins left on arduino
- 
*/

// code stored in the sketch: LaudoMobile2.ino
//Step 2: making it controllable
/*Read and took information from:
https://electrosome.com/interfacing-l298n-motor-driver-arduino-uno/
*/

/* Motor A connections: 
in1 and in2 pins are used to control the direction of Motor A
connected to pin 13, pin 12*/
int enA = 9;
int in1 = 13;
int in2 = 12;
/* Motor B connections: 
in3 and in4 pins are used to control the direction of Motor B
connected to pin 11, pin 10*/
int enB = 3;
int in3 = 11;
int in4 = 10;

//add joysick macros
#define JoyX A0
#define JoyY A1
/*if values get interfered when joysrtick readings get to 1023*/

int joyposV, joyposH;

//only runs once
void setup() {
    Serial.begin(9600);

    pinMode(JoyX, INPUT);
    pinMode(JoyY, INPUT);

    pinMode(enA, OUTPUT);
    pinMode(enB, OUTPUT);
    pinMode(in1, OUTPUT);
    pinMode(in2, OUTPUT);
    pinMode(in3, OUTPUT);
    pinMode(in4, OUTPUT);
	
    digitalWrite(in1, LOW);
    digitalWrite(in2, LOW);
    digitalWrite(in3, LOW);
    digitalWrite(in4, LOW);

    delay(1000);
    initDrive(90);

}

void loop() {
  joyposV = analogRead(JoyX);
  joyposH = analogRead(JoyY);
  
  int driveD = map(joyposV, 400, 0, 90, 255);
  int driveB = map(joyposV, 700, 1024, 90, 255);

  int driveR = map(joyposH, 400, 0, 90, 255);
  int driveL = map(joyposH, 700, 1024, 90, 255);
delay(50);


 Serial.print(joyposV);
    Serial.print("  |  ");
    Serial.print(driveD);
    Serial.print("  |  ");
    Serial.print(driveB);
    Serial.print("  |||  ");
    Serial.print(joyposH);
    Serial.print("  |  ");
    Serial.print(driveL);
    Serial.print("  |  ");
    Serial.println(driveR);
  
  //Forward and Back
  if(joyposV<400){
    //map then drive forwards
    analogWrite(enA, driveD);
    analogWrite(enB, driveD);
  delay(5);
    // motor A CW ^ (forward)
    digitalWrite(in1, LOW);
    digitalWrite(in2, HIGH);
    // motor B CW ^ (forward)
    digitalWrite(in3, HIGH);
    digitalWrite(in4, LOW);
  delay(50);
    } else if(joyposV>700){
      //moves back
    analogWrite(enA, driveB);
    analogWrite(enB, driveB);
  delay(5);
   // motor A CCW (backwards)
    digitalWrite(in1, HIGH);
    digitalWrite(in2, LOW);
  // motor B CCW (backwards)
    digitalWrite(in3, LOW);
    digitalWrite(in4, HIGH);
  delay(50);
  } else{
    // Turn off motors
    digitalWrite(in1, LOW);
    digitalWrite(in2, LOW);
    digitalWrite(in3, LOW);
    digitalWrite(in4, LOW);
  delay(50);
  }


//Rotation
  if(joyposH<400){
    //rot R
    // analogWrite(enA, driveR);
    analogWrite(enB, driveR);
  
    // motor A CCW
    digitalWrite(in1, HIGH);
    digitalWrite(in2, LOW);

    // motor B CW ^
    digitalWrite(in3, HIGH);
    digitalWrite(in4, LOW);
    delay(50);
    } else if(joyposH>700){
      //rot L
    analogWrite(enA, driveL);
    analogWrite(enB, driveL);
  
   // motor A CW ^ 
    digitalWrite(in1, LOW);
    digitalWrite(in2, HIGH);

  // motor B CCW 
    digitalWrite(in3, LOW);
    digitalWrite(in4, HIGH);
    delay(50);
  } 
  // else{
  //   // Turn off motors
  //   digitalWrite(in1, LOW);
  //   digitalWrite(in2, LOW);
  //   digitalWrite(in3, LOW);
  //   digitalWrite(in4, LOW);
  //   delay(50);
  // } //this is superfluous

}
