# Fritzing sketch LM2 (saved by Fritzing 0.9.3b)

parts:
  L298N2 = L298N DC motor driver
  Part1 = Arduino Uno (Rev3) - ICSP
  U1 = LIPO-2000mAh [package=lipo-2000]
  M1 = DC Motor
  M2 = DC Motor
  Part2 = Thumb Joystick

nets:
  N1: L298N2.OUT1, M1.pin_2
  N2: L298N2.OUT2, M1.pin_1
  N3: L298N2.OUT3, M2.pin_2
  N4: L298N2.OUT4, M2.pin_1
  N5: L298N2.12V, U1.+
  GND: L298N2.GND, Part1.GND, U1.-, Part2.GND
  5V: L298N2.5V, Part1.VIN
  N6: L298N2.ENA, Part1.D9_PWM
  N7: L298N2.ENB, Part1.D3_PWM
  N8: L298N2.IN1, Part1.D13/SCK
  N9: L298N2.IN2, Part1.D12/MISO
  N10: L298N2.IN3, Part1.D11_PWM/MOSI
  N11: L298N2.IN4, Part1.D10_PWM/SS
  N12: Part1.A0, Part2.HORZ
  N13: Part1.A1, Part2.VERT
  5V_2: Part1.5V, Part2.VCC

custom parts:
  L298N DC motor driver: 2x DC motor driver with 78M05 positive voltage regulator (7..35 V) L298N: max 46 V, 2 A Set 5 V Enable jumper to enable 5 V regultor (needed for the L298N) and +5 V output at screw terminal or supply external +5 V at screw terminal Set ENA and/or ENB to +5 V to enable motor permanently or supply ENA and/or ENB with PWM signal IN1 and IN2 set rotation directory for motor A (OUT1/OUT2) IN2 and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

// code stored in the sketch: LaudoMobile1.ino
//Laudo Lukoki
//Step 1: Make it functional
/*Read and took information from:
https://electrosome.com/interfacing-l298n-motor-driver-arduino-uno/
*/

/* Motor A connections: 
in1 and in2 pins are used to control the direction of Motor A
connected to pin 13, pin 12*/
int enA = 9;
int in1 = 13;
int in2 = 12;
/* Motor B connections: 
in3 and in4 pins are used to control the direction of Motor B
connected to pin 11, pin 10*/
int enB = 3;
int in3 = 11;
int in4 = 10;

//only runs once
void setup() {

    pinMode(enA, OUTPUT);
    pinMode(enB, OUTPUT);
    pinMode(in1, OUTPUT);
    pinMode(in2, OUTPUT);
    pinMode(in3, OUTPUT);
    pinMode(in4, OUTPUT);
	
    digitalWrite(in1, LOW);
    digitalWrite(in2, LOW);
    digitalWrite(in3, LOW);
    digitalWrite(in4, LOW);

    initDrive(100);

    // pinMode(LED_BUILTIN, OUTPUT);
    // //built in led to confirm setup function
    // digitalWrite(LED_BUILTIN, HIGH);
    // delay(1000);
    // digitalWrite(LED_BUILTIN, LOW);
    // delay(500);
    // digitalWrite(LED_BUILTIN, HIGH);
    // delay(1000);
    // digitalWrite(LED_BUILTIN, LOW);
    // delay(500);

}

void loop() {

  
  
    // directionControl();
    // delay(1000);
    // speedControl();
    // delay(1000);
}

void initDrive(int s){
  analogWrite(enA, s);
  analogWrite(enB, s);
 
  // motor A CW ^ (forward)
    digitalWrite(in1, LOW);
    digitalWrite(in2, HIGH);

  // motor B CW ^ (forward)
    digitalWrite(in3, HIGH);
    digitalWrite(in4, LOW);

    delay(1000);

 // Turn off motors
    digitalWrite(in1, LOW);
    digitalWrite(in2, LOW);
    digitalWrite(in3, LOW);
    digitalWrite(in4, LOW);
    delay(2000);


 // motor A CCW (backwards)
    digitalWrite(in1, HIGH);
    digitalWrite(in2, LOW);

  // motor B CCW ^ (backwards)
    digitalWrite(in3, LOW);
    digitalWrite(in4, HIGH);

    delay(1000);

 // Turn off motors
    digitalWrite(in1, LOW);
    digitalWrite(in2, LOW);
    digitalWrite(in3, LOW);
    digitalWrite(in4, LOW);
    delay(2000);
}


//function
void directionControl() {
    // Set motors to maximum speed
    // PWM value ranges from 0 to 255
    analogWrite(enA, 255);
    analogWrite(enB, 255);

    // Turn on motor A & B
    digitalWrite(in1, HIGH);
    digitalWrite(in2, LOW);
    digitalWrite(in3, HIGH);
    digitalWrite(in4, LOW);
    delay(2000);

    digitalWrite(in1, LOW);
    digitalWrite(in2, HIGH);
    digitalWrite(in3, LOW);
    digitalWrite(in4, HIGH);
    delay(2000);
	
    // Turn off motors
    digitalWrite(in1, LOW);
    digitalWrite(in2, LOW);
    digitalWrite(in3, LOW);
    digitalWrite(in4, LOW);
}


void speedControl() {
    // Turn on motors
    digitalWrite(in1, LOW);
    digitalWrite(in2, HIGH);
    digitalWrite(in3, LOW);
    digitalWrite(in4, HIGH);
	
    for (int i = 0; i < 256; i++) {
        analogWrite(enA, i);
        analogWrite(enB, i);
        delay(20);
    }
	
    for (int i = 255; i >= 0; --i) {
        analogWrite(enA, i);
        analogWrite(enB, i);
        delay(20);
    }
	
    // Now turn off motors
    digitalWrite(in1, LOW);
    digitalWrite(in2, LOW);
    digitalWrite(in3, LOW);
    digitalWrite(in4, LOW);
}

/*Set up function to enable wirless connection*/


/*
Concerns:
- very little pmw pins left on arduino
- 
*/

// code stored in the sketch: LaudoMobile2.ino
//Step 2: making it controllable
/*Read and took information from:
https://electrosome.com/interfacing-l298n-motor-driver-arduino-uno/
*/

/* Motor A connections: 
in1 and in2 pins are used to control the direction of Motor A
connected to pin 13, pin 12*/
int enA = 9;
int in1 = 13;
int in2 = 12;
/* Motor B connections: 
in3 and in4 pins are used to control the direction of Motor B
connected to pin 11, pin 10*/
int enB = 3;
int in3 = 11;
int in4 = 10;

//add joysick macros
#define JoyX A0
#define JoyY A1

int joyposV, joyposH;

//only runs once
void setup() {
    Serial.begin(9600);

    pinMode(JoyX, INPUT);
    pinMode(JoyY, INPUT);

    pinMode(enA, OUTPUT);
    pinMode(enB, OUTPUT);
    pinMode(in1, OUTPUT);
    pinMode(in2, OUTPUT);
    pinMode(in3, OUTPUT);
    pinMode(in4, OUTPUT);
	
    digitalWrite(in1, LOW);
    digitalWrite(in2, LOW);
    digitalWrite(in3, LOW);
    digitalWrite(in4, LOW);

    delay(1000);
    initDrive(100);

}

void loop() {
  joyposH = analogRead(JoyY);
  joyposV = analogRead(JoyX);

  int driveD = map(joyposV, 400, 0, 0, 250);
  int driveB = map(joyposV, 600, 1023, 0, 250);

  Serial.print(joyposH);
  Serial.print("  |  ");
  Serial.print(joyposV);
  Serial.print("  |  ");
  Serial.println(driveD);
  Serial.print("  |  ");
  Serial.print(driveB);

  if(joyposV<400){
    //map then drive forwards

    analogWrite(enA, driveD);
    analogWrite(enB, driveD);
  
    // motor A CW ^ (forward)
    digitalWrite(in1, LOW);
    digitalWrite(in2, HIGH);

    // motor B CW ^ (forward)
    digitalWrite(in3, HIGH);
    digitalWrite(in4, LOW);
    delay(50);
    } else if(joyposV>600){

    analogWrite(enA, driveB);
    analogWrite(enB, driveB);
  
   // motor A CCW (backwards)
    digitalWrite(in1, HIGH);
    digitalWrite(in2, LOW);

  // motor B CCW (backwards)
    digitalWrite(in3, LOW);
    digitalWrite(in4, HIGH);
  } else{
    // Turn off motors
    digitalWrite(in1, LOW);
    digitalWrite(in2, LOW);
    digitalWrite(in3, LOW);
    digitalWrite(in4, LOW);
    delay(50);
  }
  
  //map
  
  
    // directionControl();
    // delay(1000);
    // speedControl();
    // delay(1000);
}

void initDrive(int s){
  analogWrite(enA, s);
  analogWrite(enB, s);
 
  // motor A CW ^ (forward)
    digitalWrite(in1, LOW);
    digitalWrite(in2, HIGH);

  // motor B CW ^ (forward)
    digitalWrite(in3, HIGH);
    digitalWrite(in4, LOW);

    delay(500);

 // Turn off motors
    digitalWrite(in1, LOW);
    digitalWrite(in2, LOW);
    digitalWrite(in3, LOW);
    digitalWrite(in4, LOW);
    delay(1000);


 // motor A CCW (backwards)
    digitalWrite(in1, HIGH);
    digitalWrite(in2, LOW);

  // motor B CCW (backwards)
    digitalWrite(in3, LOW);
    digitalWrite(in4, HIGH);

    delay(500);

 // Turn off motors
    digitalWrite(in1, LOW);
    digitalWrite(in2, LOW);
    digitalWrite(in3, LOW);
    digitalWrite(in4, LOW);
    delay(1000);
}


//function
void directionControl() {
    // Set motors to maximum speed
    // PWM value ranges from 0 to 255
    analogWrite(enA, 255);
    analogWrite(enB, 255);

    // Turn on motor A & B
    digitalWrite(in1, HIGH);
    digitalWrite(in2, LOW);
    digitalWrite(in3, HIGH);
    digitalWrite(in4, LOW);
    delay(2000);

    digitalWrite(in1, LOW);
    digitalWrite(in2, HIGH);
    digitalWrite(in3, LOW);
    digitalWrite(in4, HIGH);
    delay(2000);
	
    // Turn off motors
    digitalWrite(in1, LOW);
    digitalWrite(in2, LOW);
    digitalWrite(in3, LOW);
    digitalWrite(in4, LOW);
}


void speedControl() {
    // Turn on motors
    digitalWrite(in1, LOW);
    digitalWrite(in2, HIGH);
    digitalWrite(in3, LOW);
    digitalWrite(in4, HIGH);
	
    for (int i = 0; i < 256; i++) {
        analogWrite(enA, i);
        analogWrite(enB, i);
        delay(20);
    }
	
    for (int i = 255; i >= 0; --i) {
        analogWrite(enA, i);
        analogWrite(enB, i);
        delay(20);
    }
	
    // Now turn off motors
    digitalWrite(in1, LOW);
    digitalWrite(in2, LOW);
    digitalWrite(in3, LOW);
    digitalWrite(in4, LOW);
}

/*
Concerns:
- very little pmw pins left on arduino
- 
*/
